# Fritzing sketch pulseOxPleth (saved by Fritzing 0.9.3b)
breadboards: 1

parts:
  Part1 = Arduino Uno (Rev3)
  OLED1 = OLED 128x64 I2C Monochrome Display
  R1 = Resistor [tolerance=±5% resistance=2.2k package="2010 [SMD]"]
  R2 = Resistor [tolerance=±5% resistance=2.2k package="2010 [SMD]"]

nets:
  N1: Part1.A4/SDA, OLED1.SDA, R2.Pin_1
  N2: Part1.A5/SCL, OLED1.SCK, R1.Pin_1
  N3: OLED1.VDD, R1.Pin_0, R2.Pin_0
